# Fritzing sketch schematic (saved by Fritzing 0.9.3b)
breadboards: 2

parts:
  Nano1 = Arduino Nano v2.3
  D1 = P1000K [part_number=P1000K]
  BAT1 = Battery Holders [package=battery-aaa]
  IC3 = SHIFT REGISTER [package=dil16]
  IC4 = SHIFT REGISTER [package=dil16]
  IC2 = SHIFT REGISTER [package=dil16]
  U1 = HEF4543 [package=dil16]
  U2 = HEF4543 [package=dil16]
  U3 = HEF4543 [package=dil16]
  U4 = HEF4543 [package=dil16]
  U5 = HEF4543 [package=dil16]
  U6 = HEF4543 [package=dil16]
  U7 = Transformer [package=transformer]
  U8 = POT [package=pot_alpha_rv16af-20]
  DI1 = 7-Segment LED Display [package=THT]
  DI2 = 7-Segment LED Display [package=THT]
  DI7 = 7-Segment LED Display [package=THT]
  DI8 = 7-Segment LED Display [package=THT]
  DI9 = 7-Segment LED Display [package=THT]
  DI10 = 7-Segment LED Display [package=THT]

nets:
  N1: Nano1.RST, IC3.SCK, IC4.SCK, IC2.SCK
  N2: Nano1.D12, D1.cathode
  VCC: Nano1.D13, IC3.SCL, IC3.VCC, IC4.SCL, IC4.VCC, IC2.SCL, IC2.VCC, U1.D0, U1.BL, U2.D0, U3.D0, U3.BL, U4.D0, U5.D0, U5.BL, U6.D0
  N3: Nano1.3V3, BAT1.-, IC3.G, IC4.G, IC2.G, U7.4
  N4: Nano1.A0, IC4.SER
  N5: Nano1.+5V, IC3.RCK, IC4.RCK, IC2.RCK
  N6: D1.anode, BAT1.+, U7.1
  GND: IC3.GND, IC4.GND, IC2.GND, U1.D, U2.D, U3.D, U4.D, U5.D, U6.D, U7.3
  N7: IC3.SER, IC2.QH*
  N8: IC4.QH*, IC2.SER
  N9: U1.D1, U2.LD, U2.BL
  N10: U1.D3, U2.D3, U2.F
  N11: U1.PH, U2.D2, U2.PH
  N12: U3.D1, U4.LD, U4.BL
  N13: U3.D3, U4.D3, U4.F
  N14: U3.PH, U4.D2, U4.PH
  N15: U5.D1, U6.LD, U6.BL
  N16: U5.D3, U6.D3, U6.F
  N17: U5.PH, U6.D2, U6.PH
  N18: U7.2, U8.E
  N19: U8.S, DI1.commAnode, DI2.commAnode, DI7.cathodeA, DI7.commAnode, DI8.cathodeA, DI8.commAnode, DI9.cathodeA, DI9.commAnode, DI10.cathodeA, DI10.commAnode
